# Fritzing sketch mcp_thermistor (saved by Fritzing 0.9.3b)
breadboards: 1

parts:
  Part1 = Arduino Uno (Rev3)
  R1 = Temperature Sensor (Thermistor) [thermistor_type=NTC package=THT]
  R2 = Resistor [tolerance=±5% resistance=220 package=THT]

nets:
  N1: Part1.A0, R1.pin_1, R2.Pin_0
  N2: Part1.AREF, Part1.3V3, R2.Pin_1
  N3: Part1.GND, R1.pin_0

notes:
  @mathcodeprint
